# Fritzing sketch NailsAndTransistorBackupRecovered (saved by Fritzing 0.9.9b)
breadboards: 1

parts:
  Part1 = Adafruit Feather HUZZAH ESP8266 [part_number="Adafruit #2821"]
  Q1 = TRANSISTOR_NPN [package=to-92-ammo]
  R1 = Resistor [tolerance=±5% power=0.25 resistance=220 package=THT]
  R2 = Resistor [tolerance=±5% power=0.25 resistance=220 package=THT]
  R3 = Resistor [tolerance=±5% power=0.25 resistance=200 package=THT]

nets:
  N1: Part1.GPIO13/MOSI, Q1.B
  N2: Part1.ADC, R2.Pin_1, R3.Pin_0
  N3: Part1.GND, R2.Pin_0
  N4: Part1.3.3V, R1.Pin_1
  N5: Q1.C, R1.Pin_0

notes:
  Nail

custom parts:
  Adafruit Feather HUZZAH ESP8266: his is the Adafruit Feather HUZZAH ESP8266 - our take on an 'all-in-one' ESP8266 WiFi development board with built in USB and battery charging. Its an ESP8266 WiFi module with all the extras you need, ready to rock! We have other boards in the Feather family, check'em out here. At the Feather HUZZAH's heart is an ESP8266 WiFi microcontroller clocked at 80 MHz and at 3.3V logic. This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
