# Fritzing sketch NailsAndTransistorDigitallyControlled (saved by Fritzing 0.9.9b)
breadboards: 1

parts:
  Part2 = Adafruit Feather HUZZAH ESP8266 [part_number="Adafruit #2821"]
  R5 = Resistor [tolerance=±5% power=0.25 resistance=10000 package=THT]
  R6 = Resistor [tolerance=±5% power=0.25 resistance=220 package=THT]

nets:
  N1: Part2.ADC, R5.Pin_1, R6.Pin_0
  N2: Part2.GND, R5.Pin_0

notes:
  Nail

custom parts:
  Adafruit Feather HUZZAH ESP8266: his is the Adafruit Feather HUZZAH ESP8266 - our take on an 'all-in-one' ESP8266 WiFi development board with built in USB and battery charging. Its an ESP8266 WiFi module with all the extras you need, ready to rock! We have other boards in the Feather family, check'em out here. At the Feather HUZZAH's heart is an ESP8266 WiFi microcontroller clocked at 80 MHz and at 3.3V logic. This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
